// Logisim project lab2_I_delavega_rev_2.circ as structural Verilog: 1 circuit, main circuit main
module main (
  input  A,
  input  in_2,
  input  E,
  input  B,
  input  C,
  input  D,
  output out_7
);

  wire and_1_out, and_2_out, and_3_out, or_1_out, or_2_out;

  and and_1 (and_1_out, A, in_2);
  or or_1 (or_1_out, and_1_out, and_1_out);
  and and_2 (and_2_out, B, C);
  or or_2 (or_2_out, or_1_out, E);
  and and_3 (and_3_out, and_2_out, D);
  or or_3 (out_7, or_2_out, and_3_out);
endmodule
