// Logisim project week5.circ as structural Verilog: 1 circuit, main circuit main
module main (
  input  A,
  input  B,
  input  F0,
  input  F1,
  input  F2,
  output out_6
);

  wire and_1_out, and_2_out, and_3_out, and_4_out, and_5_out, and_6_out, and_7_out, and_8_out, and_9_out,
       and_10_out, and_11_out, not_1_out, not_2_out, or_1_out, xor_1_out;

  not not_1 (not_1_out, A);
  not not_2 (not_2_out, B);
  xor xor_1 (xor_1_out, A, B);
  and and_1 (and_1_out, A, B);
  or or_1 (or_1_out, A, B);
  and and_2 (and_2_out, F2, F1, F0);
  and and_3 (and_3_out, F2, F1, F0);
  and and_4 (and_4_out, F2, F1, F0);
  and and_5 (and_5_out, F2, F1, F0);
  and and_6 (and_6_out, F2, F1, F0);
  and and_7 (and_7_out, xor_1_out, and_2_out);
  and and_8 (and_8_out, and_1_out, and_3_out);
  and and_9 (and_9_out, or_1_out, and_4_out);
  and and_10 (and_10_out, not_1_out, and_5_out);
  and and_11 (and_11_out, not_2_out, and_6_out);
  or or_2 (out_6, and_7_out, and_8_out, and_9_out, and_10_out, and_11_out);
endmodule
