// Logisim project problem2_4_A_rev_a.circ as structural Verilog: 1 circuit, main circuit main
module main (
  input  A,
  input  B,
  input  E,
  input  B1,
  input  C,
  input  D,
  output F
);

  wire and_1_out, and_2_out, and_3_out, or_1_out, or_2_out;

  and and_1 (and_1_out, A, B);
  and and_2 (and_2_out, B1, C);
  or or_1 (or_1_out, and_1_out, and_1_out);
  and and_3 (and_3_out, and_2_out, D);
  or or_2 (or_2_out, or_1_out, E);
  or or_3 (F, or_2_out, and_3_out);
endmodule
