// Logisim project problem_2_4_B_rev_a.circ as structural Verilog: 1 circuit, main circuit main
module main (
  input  A,
  input  B,
  input  B1,
  input  B3,
  input  A1,
  input  A2,
  input  B2,
  output out_8
);

  wire and_1_out, and_2_out, and_3_out, not_1_out, or_1_out, or_2_out;

  not not_1 (not_1_out, B);
  and and_1 (and_1_out, A1, B2);
  and and_2 (and_2_out, A, not_1_out);
  or or_1 (or_1_out, B1, and_1_out);
  or or_2 (or_2_out, and_2_out, or_1_out);
  and and_3 (and_3_out, or_2_out, B3);
  or or_3 (out_8, and_3_out, A2);
endmodule
